// Logisim project Angelo_Eduardo_Marco_Vinicius_5-bit_multiplier.circ as structural Verilog: 10 circuits, main circuit Main
module Main (
  input  [4:0] in_1,
  input  [4:0] in_2,
  output [9:0] produto_P
);

  wire a1_t, a2_t, a3_t, a4_t, a5, a6, a7, a8, a9, b1_t, b2_t, b3_t, b4_t, b5, b6, b7, b8, b9, c1, c2, c3,
       c4, c5, c6, c7, c8, c9, d1, d2, d3, d4, d5, d6, d7, d8, d9, e1, e2, e3, e4, e5, e6, e7, e8, e9, f1,
       f2, f3, f4, f5, f6, f7, f8, f9, g1, g2, g3, g4, g5, g6, g7, g8, g9;

  _7_Segment_Display u_7_segment_display_1 (.g(g3), .f(f3), .a(a3_t), .b(b3_t), .e(e3), .d(d3), .c(c3));  // open: dp
  // Probe on in_1
  _7_Segment_Display u_7_segment_display_2 (.g(g2), .f(f2), .a(a2_t), .b(b2_t), .e(e2), .d(d2), .c(c2));  // open: dp
  _7_Segment_Display u_7_segment_display_3 (.g(g1), .f(f1), .a(a1_t), .b(b1_t), .e(e1), .d(d1), .c(c1));  // open: dp
  _7_Segment_Display u_7_segment_display_4 (.g(g9), .f(f9), .a(a9), .b(b9), .e(e9), .d(d9), .c(c9));  // open: dp
  // Probe on in_2
  _7_Segment_Display u_7_segment_display_5 (.g(g8), .f(f8), .a(a8), .b(b8), .e(e8), .d(d8), .c(c8));  // open: dp
  _7_Segment_Display u_7_segment_display_6 (.g(g7), .f(f7), .a(a7), .b(b7), .e(e7), .d(d7), .c(c7));  // open: dp
  // Probe on produto_P
  _7_Segment_Display u_7_segment_display_7 (.g(g6), .f(f6), .a(a6), .b(b6), .e(e6), .d(d6), .c(c6));  // open: dp
  _7_Segment_Display u_7_segment_display_8 (.g(g5), .f(f5), .a(a5), .b(b5), .e(e5), .d(d5), .c(c5));  // open: dp
  _7_Segment_Display u_7_segment_display_9 (.g(g4), .f(f4), .a(a4_t), .b(b4_t), .e(e4), .d(d4), .c(c4));  // open: dp

  // Other names for the same wires on the sheet: A[4:0] = in_1; A0 = in_1[0]; A1 = in_1[1]; A2 = in_1[2];
  //   A3 = in_1[3]; A4 = in_1[4]; B[4:0] = in_2; B0 = in_2[0]; B1 = in_2[1]; B2 = in_2[2]; B3 = in_2[3]; B4 = in_2[4];
  //   P[9:0] = produto_P; P0 = produto_P[0]; P1 = produto_P[1]; P2 = produto_P[2]; P3 = produto_P[3];
  //   P4 = produto_P[4]; P5 = produto_P[5]; P6 = produto_P[6]; P7 = produto_P[7]; P8 = produto_P[8];
  //   P9 = produto_P[9]

  // Notes on the sheet:
  //   Aluno 1: Angelo da Silva Viero
  //   Aluno 2: Eduardo Zitske
  //   Aluno 3: Marco Antonio Cattelan
  //   Aluno 4: Vinicius Rocca
  //   Atenção: é obrigatório utilizar, em qualquer trabalho escolhido, as construções abaixo para informar os valores de 5 bits dos operandos e verificar o produto de 10 bits.
  //   [OPCIONAL] Exemplo de organização para as opções que envolverem displays (apagar se a opção do grupo não envolver displays):
  //   Centena
  //   operando A
  //   Dezena
  //   Unidade
  //   X
  //   operando B
  //   Centena
  //   Informe o trabalho escolhido, apagando os demais:
  //   Multiplicador Array 5 bits + displays 7 segmentos
  //   Dezena
  //   Unidade
  //   Centena
  //   Dezena
  //   01/2018
  //   Unidade
endmodule

module Main_Multi (
  input  [4:0] B,
  input  [4:0] A,
  output out_3,
  output out_4,
  output out_5,
  output out_6,
  output out_7,
  output out_8,
  output out_9,
  output out_10,
  output out_11,
  output out_12
);

  wire Carry_S1, Carry_S2, Carry_S3, LSB_M1, LSB_M2, LSB_M3, LSB_M4, LSB_M5, M12, M13, M14, M22, M23, M24,
       M32, M33, M34, M42, M43, M44, M52, M53, M54, MSB_M1, MSB_M2, MSB_M3, MSB_M4, MSB_M5, MSB_S1, MSB_S2,
       MSB_S3, S12, S13, S14, S15, S22, S23, S24, S25, S32, S33, S34, S35;

  TrabalhoCD_FUNC_Multiplicator multiplicator_1 (
    .IN0(A[0]), .IN1(B[0]), .IN2(B[1]), .IN3(B[2]), .IN4(B[3]), .IN5(B[4]), .OUT5(MSB_M1), .OUT4(M14),
    .OUT3(M13), .OUT2(M12), .OUT1(LSB_M1));
  TrabalhoCD_FUNC_Multiplicator multiplicator_2 (
    .IN0(A[1]), .IN1(B[0]), .IN2(B[1]), .IN3(B[2]), .IN4(B[3]), .IN5(B[4]), .OUT5(MSB_M2), .OUT4(M24),
    .OUT3(M23), .OUT2(M22), .OUT1(LSB_M2));
  TrabalhoCD_FUNC_Multiplicator multiplicator_3 (
    .IN0(A[2]), .IN1(B[0]), .IN2(B[1]), .IN3(B[2]), .IN4(B[3]), .IN5(B[4]), .OUT5(MSB_M3), .OUT4(M34),
    .OUT3(M33), .OUT2(M32), .OUT1(LSB_M3));
  TrabalhoCD_FUNC_Multiplicator multiplicator_4 (
    .IN0(A[3]), .IN1(B[0]), .IN2(B[1]), .IN3(B[2]), .IN4(B[3]), .IN5(B[4]), .OUT5(MSB_M4), .OUT4(M44),
    .OUT3(M43), .OUT2(M42), .OUT1(LSB_M4));
  TrabalhoCD_FUNC_Multiplicator multiplicator_5 (
    .IN0(A[4]), .IN1(B[0]), .IN2(B[1]), .IN3(B[2]), .IN4(B[3]), .IN5(B[4]), .OUT5(MSB_M5), .OUT4(M54),
    .OUT3(M53), .OUT2(M52), .OUT1(LSB_M5));
  TrabalhoCD_FUNC_Sum sum_1 (
    .IN00(LSB_M1), .IN01(M12), .IN02(M13), .IN03(M14), .IN04(MSB_M1), .IN05(1'b0), .IN11(LSB_M2), .IN12(M22),
    .IN13(M23), .IN14(M24), .IN15(MSB_M2), .F_OUT(out_12), ._1_OUT(S12), ._2_OUT(S13), ._3_OUT(S14),
    ._4_OUT(S15), ._5_OUT(MSB_S1), ._6_OUT(Carry_S1));
  TrabalhoCD_FUNC_Sum sum_2 (
    .IN00(S12), .IN01(S13), .IN02(S14), .IN03(S15), .IN04(MSB_S1), .IN05(Carry_S1), .IN11(LSB_M3),
    .IN12(M32), .IN13(M33), .IN14(M34), .IN15(MSB_M3), .F_OUT(out_11), ._1_OUT(S22), ._2_OUT(S23),
    ._3_OUT(S24), ._4_OUT(S25), ._5_OUT(MSB_S2), ._6_OUT(Carry_S2));
  TrabalhoCD_FUNC_Sum sum_3 (
    .IN00(S22), .IN01(S23), .IN02(S24), .IN03(S25), .IN04(MSB_S2), .IN05(Carry_S2), .IN11(LSB_M4),
    .IN12(M42), .IN13(M43), .IN14(M44), .IN15(MSB_M4), .F_OUT(out_10), ._1_OUT(S32), ._2_OUT(S33),
    ._3_OUT(S34), ._4_OUT(S35), ._5_OUT(MSB_S3), ._6_OUT(Carry_S3));
  TrabalhoCD_FUNC_Sum sum_4 (
    .IN00(S32), .IN01(S33), .IN02(S34), .IN03(S35), .IN04(MSB_S3), .IN05(Carry_S3), .IN11(LSB_M5),
    .IN12(M52), .IN13(M53), .IN14(M54), .IN15(MSB_M5), .F_OUT(out_9), ._1_OUT(out_8), ._2_OUT(out_7),
    ._3_OUT(out_6), ._4_OUT(out_5), ._5_OUT(out_4), ._6_OUT(out_3));

  // Other names for the same wires on the sheet: LSB_A = A[0]; A2 = A[1]; A3 = A[2]; A4 = A[3]; MSB_A = A[4];
  //   LSB_B = B[0]; B2 = B[1]; B3 = B[2]; B4 = B[3]; MSB_B = B[4]; LSB = out_12; MSB = out_3; O2 = out_11;
  //   O3 = out_10; O4 = out_9; O5 = out_8; O6 = out_7; O7 = out_6; O8 = out_5; O9 = out_4
endmodule

module Sum (
  input  IN00,
  input  IN01,
  input  IN02,
  input  IN03,
  input  IN04,
  input  IN05,
  input  IN11,
  input  IN12,
  input  IN13,
  input  IN14,
  input  IN15,
  output F_OUT,
  output _1_OUT,
  output _2_OUT,
  output _3_OUT,
  output _4_OUT,
  output _5_OUT,
  output _6_OUT
);

  wire full_adder_1_carry_out, full_adder_2_carry_out, full_adder_3_carry_out, half_adder_1_p1;

  TrabalhoCD_FUNC_Half_Adder half_adder_1 (.A(IN01), .B(IN11), .P0(_1_OUT), .P1(half_adder_1_p1));
  TrabalhoCD_FUNC_Full_Adder full_adder_1 (
    .Carry_IN(half_adder_1_p1), .A(IN02), .B(IN12), .S(_2_OUT), .Carry_OUT(full_adder_1_carry_out));
  TrabalhoCD_FUNC_Full_Adder full_adder_2 (
    .Carry_IN(full_adder_1_carry_out), .A(IN03), .B(IN13), .S(_3_OUT), .Carry_OUT(full_adder_2_carry_out));
  TrabalhoCD_FUNC_Full_Adder full_adder_3 (
    .Carry_IN(full_adder_2_carry_out), .A(IN04), .B(IN14), .S(_4_OUT), .Carry_OUT(full_adder_3_carry_out));
  TrabalhoCD_FUNC_Full_Adder full_adder_4 (
    .Carry_IN(full_adder_3_carry_out), .A(IN05), .B(IN15), .S(_5_OUT), .Carry_OUT(_6_OUT));

  assign F_OUT = IN00;
endmodule

module Multiplicator (
  input  IN0,
  input  IN1,
  input  IN2,
  input  IN3,
  input  IN4,
  input  IN5,
  output OUT5,
  output OUT4,
  output OUT3,
  output OUT2,
  output OUT1
);

  and and_1 (OUT1, IN1, IN0);
  and and_2 (OUT2, IN2, IN0);
  and and_3 (OUT3, IN3, IN0);
  and and_4 (OUT4, IN4, IN0);
  and and_5 (OUT5, IN5, IN0);
endmodule

module Half_Adder (
  input  A,
  input  B,
  output P0,
  output P1
);

  xor xor_1 (P0, A, B);
  and and_1 (P1, A, B);
endmodule

module Full_Adder (
  input  Carry_IN,
  input  A,
  input  B,
  output S,
  output Carry_OUT
);

  wire and_1_out, and_2_out, xor_1_out;

  and and_1 (and_1_out, A, B);
  xor xor_1 (xor_1_out, A, B);
  xor xor_2 (S, Carry_IN, xor_1_out);
  and and_2 (and_2_out, Carry_IN, xor_1_out);
  or or_1 (Carry_OUT, and_2_out, and_1_out);
endmodule

module Main_Displ (
  input  _9,
  input  _8,
  input  _7,
  input  _6,
  input  _5,
  input  _4,
  input  _3,
  input  _2,
  input  _1,
  input  _0,
  output aU,
  output bU,
  output cU,
  output dU,
  output eU,
  output fU,
  output gU,
  output aD,
  output bD,
  output cD,
  output dD,
  output eD,
  output fD,
  output gD,
  output aC,
  output bC,
  output cC,
  output dC,
  output eC,
  output fC,
  output gC
);

  wire binary_to_bcd_1_p6, binary_to_bcd_2_p2, binary_to_bcd_3_p2, binary_to_bcd_7_p1, binary_to_bcd_8_p4,
       binary_to_bcd_9_p1, binary_to_bcd_9_p2, binary_to_bcd_12_p1, binary_to_bcd_12_p2, binary_to_bcd_12_p3,
       binary_to_bcd_12_p4, binary_to_bcd_12_p5, binary_to_bcd_13_p1, binary_to_bcd_15_p1,
       binary_to_bcd_15_p2, binary_to_bcd_15_p3, binary_to_bcd_15_p4;

  // Binary_to_bcd binary_to_bcd_1: pin names not known; wires that end beside it: _9, 1'b0, 1'b0, 1'b0, _8, binary_to_bcd_1_p6
  // Binary_to_bcd binary_to_bcd_2: pin names not known; wires that end beside it: _6, binary_to_bcd_2_p2
  // Binary_to_bcd binary_to_bcd_3: pin names not known; wires that end beside it: _7, binary_to_bcd_3_p2
  // Binary_to_bcd binary_to_bcd_4: pin names not known; wires that end beside it: _3
  // Binary_to_bcd binary_to_bcd_5: pin names not known; wires that end beside it: _4
  // Binary_to_bcd binary_to_bcd_6: pin names not known; wires that end beside it: _5
  // Binary_to_bcd binary_to_bcd_7: pin names not known; wires that end beside it: binary_to_bcd_7_p1
  // Binary_to_bcd binary_to_bcd_8: pin names not known; wires that end beside it: binary_to_bcd_2_p2, binary_to_bcd_3_p2, binary_to_bcd_1_p6, binary_to_bcd_8_p4
  // Binary_to_bcd binary_to_bcd_9: pin names not known; wires that end beside it: binary_to_bcd_9_p1, binary_to_bcd_9_p2
  // Binary_to_bcd binary_to_bcd_10: pin names not known; wires that end beside it: _1
  // Binary_to_bcd binary_to_bcd_11: pin names not known; wires that end beside it: _2
  // Binary_to_bcd binary_to_bcd_12: pin names not known; wires that end beside it: binary_to_bcd_12_p1, binary_to_bcd_12_p2, binary_to_bcd_12_p3, binary_to_bcd_12_p4, binary_to_bcd_12_p5
  // Binary_to_bcd binary_to_bcd_13: pin names not known; wires that end beside it: binary_to_bcd_13_p1, binary_to_bcd_7_p1, binary_to_bcd_8_p4
  // Binary_to_bcd binary_to_bcd_14: pin names not known; wires that end beside it: binary_to_bcd_13_p1
  // Binary_to_bcd binary_to_bcd_15: pin names not known; wires that end beside it: binary_to_bcd_15_p1, binary_to_bcd_15_p2, binary_to_bcd_15_p3, binary_to_bcd_15_p4
  // TrabalhoCD_FUNC_7_Seg__Displ__2 7_seg_displ_2_1: pin names not known; wires that end beside it: binary_to_bcd_12_p1, binary_to_bcd_9_p2, binary_to_bcd_9_p1, _0, aU, bU, cU, dU, eU, fU, gU
  // TrabalhoCD_FUNC_7_Seg__Displ 7_seg_displ_1: pin names not known; wires that end beside it: binary_to_bcd_12_p5, binary_to_bcd_12_p4, binary_to_bcd_12_p3, binary_to_bcd_12_p2, aD, bD, cD, dD, eD, fD, gD
  // TrabalhoCD_FUNC_7_Seg__Displ 7_seg_displ_2: pin names not known; wires that end beside it: binary_to_bcd_15_p4, binary_to_bcd_15_p3, binary_to_bcd_15_p2, binary_to_bcd_15_p1, aC, bC, cC, dC, eC, fC, gC

  // Notes on the sheet:
  //   UNIDADE
  //   DEZENA
  //   CENTENA
endmodule

module _7_Seg__Displ (
  input  O4,
  input  O3,
  input  O2,
  input  LSB,
  output a,
  output b,
  output c,
  output d,
  output e,
  output f,
  output g
);

  wire and_1_out, and_2_out, and_3_out, and_4_out, and_5_out, and_6_out, and_7_out, and_8_out, and_9_out,
       and_10_out, and_11_out, and_12_out, and_13_out, and_14_out, and_15_out, and_16_out, and_17_out,
       and_18_out, and_19_out, and_20_out, and_21_out, and_22_out, and_23_out, and_24_out, and_25_out,
       and_26_out, and_27_out, not_1_out, not_2_out, not_3_out, not_4_out, not_5_out, not_6_out, not_7_out,
       not_8_out, not_9_out, not_10_out, not_11_out, not_12_out, not_13_out, not_14_out, not_15_out,
       not_16_out, not_17_out, not_18_out, not_19_out, not_20_out, not_21_out, not_22_out, not_23_out,
       not_24_out, not_25_out, not_26_out, not_27_out, not_28_out, not_29_out, not_30_out, not_31_out,
       not_32_out, not_33_out;

  not not_1 (not_1_out, O3);
  and and_1 (and_1_out, not_1_out, not_2_out);
  not not_2 (not_2_out, LSB);
  and and_2 (and_2_out, O3, LSB);
  not not_3 (not_3_out, O4);
  and and_3 (and_3_out, not_3_out, not_4_out);
  not not_4 (not_4_out, O3);
  not not_5 (not_5_out, O4);
  not not_6 (not_6_out, O2);
  and and_4 (and_4_out, not_5_out, not_6_out, not_7_out);
  not not_7 (not_7_out, LSB);
  not not_8 (not_8_out, O3);
  and and_5 (and_5_out, not_8_out, LSB);
  not not_9 (not_9_out, O3);
  and and_6 (and_6_out, not_9_out, O2);
  and and_7 (and_7_out, O2, LSB);
  and and_8 (and_8_out, O4, O3);
  not not_10 (not_10_out, O2);
  not not_11 (not_11_out, O3);
  and and_9 (and_9_out, not_11_out, not_12_out, not_13_out);
  not not_12 (not_12_out, O2);
  not not_13 (not_13_out, LSB);
  not not_14 (not_14_out, O4);
  and and_10 (and_10_out, not_14_out, O2, not_15_out);
  not not_15 (not_15_out, LSB);
  not not_16 (not_16_out, O3);
  and and_11 (and_11_out, not_16_out, O2, LSB);
  not not_17 (not_17_out, O2);
  and and_12 (and_12_out, O3, not_17_out, LSB);
  and and_13 (and_13_out, O4, not_18_out, not_19_out);
  not not_18 (not_18_out, O2);
  not not_19 (not_19_out, LSB);
  and and_14 (and_14_out, O4, O3, LSB);
  not not_20 (not_20_out, O4);
  and and_15 (and_15_out, not_20_out, not_21_out, not_22_out);
  not not_21 (not_21_out, O3);
  not not_22 (not_22_out, LSB);
  not not_23 (not_23_out, O4);
  and and_16 (and_16_out, not_23_out, O2, not_24_out);
  not not_24 (not_24_out, LSB);
  and and_17 (and_17_out, O4, O2, LSB);
  and and_18 (and_18_out, O4, O3, LSB);
  not not_25 (not_25_out, O2);
  and and_19 (and_19_out, not_25_out, not_26_out);
  not not_26 (not_26_out, LSB);
  and and_20 (and_20_out, O3, not_27_out);
  not not_27 (not_27_out, O2);
  and and_21 (and_21_out, O3, not_28_out);
  not not_28 (not_28_out, LSB);
  and and_22 (and_22_out, O4, LSB);
  not not_29 (not_29_out, O4);
  and and_23 (and_23_out, not_29_out, not_30_out, O2);
  not not_30 (not_30_out, O3);
  and and_24 (and_24_out, O3, not_31_out);
  not not_31 (not_31_out, O2);
  and and_25 (and_25_out, O3, not_32_out);
  not not_32 (not_32_out, LSB);
  and and_26 (and_26_out, O4, not_33_out);
  not not_33 (not_33_out, O2);
  and and_27 (and_27_out, O4, LSB);
  or or_1 (a, and_1_out, O2, and_2_out, O4);
  or or_2 (c, not_10_out, LSB, O3, O4);
  or or_3 (e, and_15_out, and_16_out, and_17_out, and_18_out);
  or or_4 (f, and_19_out, and_20_out, and_21_out, and_22_out);
  or or_5 (g, and_23_out, and_24_out, and_25_out, and_26_out, and_27_out);
  or or_6 (b, and_3_out, and_4_out, and_5_out, and_6_out, and_7_out, and_8_out);
  or or_7 (d, and_9_out, and_10_out, and_11_out, and_12_out, and_13_out, and_14_out);
endmodule

module Binary_to_BCD (
  input  LSB,
  input  O2,
  input  O3,
  input  O4,
  output LSBF,
  output O2F,
  output O3F,
  output O4F
);

  wire and_1_out, and_2_out, and_3_out, and_4_out, and_5_out, and_6_out, and_7_out, and_8_out, and_9_out,
       and_10_out, not_1_out, not_2_out, not_3_out, not_4_out, not_5_out, not_6_out, not_7_out, not_8_out;

  not not_1 (not_1_out, LSB);
  and and_1 (and_1_out, not_1_out, O4);
  not not_2 (not_2_out, LSB);
  and and_2 (and_2_out, not_2_out, O2, O3);
  and and_3 (and_3_out, LSB, not_3_out, not_4_out);
  not not_3 (not_3_out, O3);
  not not_4 (not_4_out, O4);
  not not_5 (not_5_out, LSB);
  and and_4 (and_4_out, not_5_out, O4);
  and and_5 (and_5_out, O2, not_6_out);
  not not_6 (not_6_out, O3);
  and and_6 (and_6_out, LSB, O2);
  not not_7 (not_7_out, LSB);
  not not_8 (not_8_out, O2);
  and and_7 (and_7_out, not_7_out, not_8_out, O3);
  and and_8 (and_8_out, LSB, O4);
  and and_9 (and_9_out, O2, O3);
  and and_10 (and_10_out, LSB, O3);
  or or_1 (LSBF, and_1_out, and_2_out, and_3_out);
  or or_2 (O2F, and_4_out, and_5_out, and_6_out);
  or or_3 (O3F, and_7_out, and_8_out);
  or or_4 (O4F, O4, and_9_out, and_10_out);
endmodule

module _7_Seg__Displ__2 (
  input  O4,
  input  O3,
  input  O2,
  input  LSB,
  output a,
  output b,
  output c,
  output d,
  output e,
  output f,
  output g
);

  wire and_1_out, and_2_out, and_3_out, and_4_out, and_5_out, and_6_out, and_7_out, and_8_out, and_9_out,
       and_10_out, and_11_out, and_12_out, and_13_out, and_14_out, and_15_out, and_16_out, and_17_out,
       and_18_out, and_19_out, and_20_out, and_21_out, and_22_out, and_23_out, not_1_out, not_2_out,
       not_3_out, not_4_out, not_5_out, not_6_out, not_7_out, not_8_out, not_9_out, not_10_out, not_11_out,
       not_12_out, not_13_out, not_14_out, not_15_out, not_16_out, not_17_out, not_18_out, not_19_out,
       not_20_out, not_21_out, not_22_out, not_23_out, not_24_out, not_25_out, not_26_out, not_27_out,
       not_28_out, not_29_out;

  not not_1 (not_1_out, O3);
  and and_1 (and_1_out, not_1_out, not_2_out);
  not not_2 (not_2_out, LSB);
  and and_2 (and_2_out, O3, LSB);
  not not_3 (not_3_out, O3);
  not not_4 (not_4_out, O2);
  and and_3 (and_3_out, not_4_out, not_5_out);
  not not_5 (not_5_out, LSB);
  and and_4 (and_4_out, O2, LSB);
  not not_6 (not_6_out, O2);
  not not_7 (not_7_out, O3);
  not not_8 (not_8_out, O2);
  and and_5 (and_5_out, not_7_out, not_8_out, not_9_out);
  not not_9 (not_9_out, LSB);
  not not_10 (not_10_out, O4);
  and and_6 (and_6_out, not_10_out, O2, not_11_out);
  not not_11 (not_11_out, LSB);
  not not_12 (not_12_out, O3);
  and and_7 (and_7_out, not_12_out, O2, LSB);
  not not_13 (not_13_out, O2);
  and and_8 (and_8_out, O3, not_13_out, LSB);
  not not_14 (not_14_out, O2);
  and and_9 (and_9_out, O4, not_14_out, not_15_out);
  not not_15 (not_15_out, LSB);
  and and_10 (and_10_out, O4, O3, LSB);
  not not_16 (not_16_out, O3);
  and and_11 (and_11_out, not_16_out, not_17_out, not_18_out);
  not not_17 (not_17_out, O2);
  not not_18 (not_18_out, LSB);
  not not_19 (not_19_out, O4);
  and and_12 (and_12_out, not_19_out, O2, not_20_out);
  not not_20 (not_20_out, LSB);
  and and_13 (and_13_out, O4, O2, LSB);
  and and_14 (and_14_out, O4, O3, LSB);
  not not_21 (not_21_out, O2);
  and and_15 (and_15_out, not_21_out, not_22_out);
  not not_22 (not_22_out, LSB);
  and and_16 (and_16_out, O3, not_23_out);
  not not_23 (not_23_out, O2);
  and and_17 (and_17_out, O3, not_24_out);
  not not_24 (not_24_out, LSB);
  and and_18 (and_18_out, O4, LSB);
  not not_25 (not_25_out, O4);
  not not_26 (not_26_out, O3);
  and and_19 (and_19_out, not_25_out, not_26_out, O2);
  and and_20 (and_20_out, O3, not_27_out);
  not not_27 (not_27_out, O2);
  and and_21 (and_21_out, O3, not_28_out);
  not not_28 (not_28_out, LSB);
  and and_22 (and_22_out, O4, not_29_out);
  not not_29 (not_29_out, O2);
  and and_23 (and_23_out, O4, LSB);
  or or_1 (a, and_1_out, O2, and_2_out, O4);
  or or_2 (b, not_3_out, and_3_out, and_4_out, O4);
  or or_3 (c, not_6_out, LSB, O3, O4);
  or or_4 (e, and_11_out, and_12_out, and_13_out, and_14_out);
  or or_5 (f, and_15_out, and_16_out, and_17_out, and_18_out);
  or or_6 (g, and_19_out, and_20_out, and_21_out, and_22_out, and_23_out);
  or or_7 (d, and_5_out, and_6_out, and_7_out, and_8_out, and_9_out, and_10_out);
endmodule
