// Logisim project Binary to BCD implement.circ as structural Verilog: 5 circuits, main circuit main
module main (
  input  _9,
  input  _8,
  input  _7,
  input  _6,
  input  _5,
  input  _4,
  input  _3,
  input  _2,
  input  _1,
  input  _0,
  output aU,
  output bU,
  output cU,
  output dU,
  output eU,
  output fU,
  output gU,
  output aD,
  output bD,
  output cD,
  output dD,
  output eD,
  output fD,
  output gD,
  output aC,
  output bC,
  output cC,
  output dC,
  output eC,
  output fC,
  output gC
);

  wire binary_to_bcd_2_0_1_lsbf, binary_to_bcd_2_0_1_o2f, binary_to_bcd_2_0_1_o3f, binary_to_bcd_2_0_1_o4f,
       binary_to_bcd_2_0_2_lsbf, binary_to_bcd_2_0_2_o2f, binary_to_bcd_2_0_2_o3f, binary_to_bcd_2_0_2_o4f,
       binary_to_bcd_2_0_3_lsbf, binary_to_bcd_2_0_3_o2f, binary_to_bcd_2_0_3_o3f, binary_to_bcd_2_0_3_o4f,
       binary_to_bcd_2_0_4_lsbf, binary_to_bcd_2_0_4_o2f, binary_to_bcd_2_0_4_o3f, binary_to_bcd_2_0_4_o4f,
       binary_to_bcd_2_0_5_lsbf, binary_to_bcd_2_0_5_o2f, binary_to_bcd_2_0_5_o3f, binary_to_bcd_2_0_5_o4f,
       binary_to_bcd_2_0_6_lsbf, binary_to_bcd_2_0_6_o2f, binary_to_bcd_2_0_6_o3f, binary_to_bcd_2_0_6_o4f,
       binary_to_bcd_2_0_7_lsbf, binary_to_bcd_2_0_7_o2f, binary_to_bcd_2_0_7_o3f, binary_to_bcd_2_0_7_o4f,
       binary_to_bcd_2_0_8_lsbf, binary_to_bcd_2_0_8_o2f, binary_to_bcd_2_0_8_o3f, binary_to_bcd_2_0_8_o4f,
       binary_to_bcd_2_0_9_lsbf, binary_to_bcd_2_0_9_o2f, binary_to_bcd_2_0_9_o3f, binary_to_bcd_2_0_9_o4f,
       binary_to_bcd_2_0_10_lsbf, binary_to_bcd_2_0_10_o2f, binary_to_bcd_2_0_10_o3f,
       binary_to_bcd_2_0_10_o4f, binary_to_bcd_2_0_11_lsbf, binary_to_bcd_2_0_11_o2f,
       binary_to_bcd_2_0_11_o3f, binary_to_bcd_2_0_11_o4f, binary_to_bcd_2_0_12_lsbf,
       binary_to_bcd_2_0_12_o2f, binary_to_bcd_2_0_12_o3f, binary_to_bcd_2_0_12_o4f,
       binary_to_bcd_2_0_13_lsbf, binary_to_bcd_2_0_13_o2f, binary_to_bcd_2_0_13_o3f,
       binary_to_bcd_2_0_13_o4f, binary_to_bcd_2_0_14_lsbf, binary_to_bcd_2_0_14_o2f,
       binary_to_bcd_2_0_14_o3f, binary_to_bcd_2_0_14_o4f, binary_to_bcd_2_0_15_lsbf,
       binary_to_bcd_2_0_15_o2f, binary_to_bcd_2_0_15_o3f;

  Binary_to_bcd_2_0 binary_to_bcd_2_0_1 (
    .LSB(_9), .O2(1'b0), .O3(1'b0), .O4(1'b0), .LSBF(binary_to_bcd_2_0_1_lsbf),
    .O2F(binary_to_bcd_2_0_1_o2f), .O3F(binary_to_bcd_2_0_1_o3f), .O4F(binary_to_bcd_2_0_1_o4f));
  Binary_to_bcd_2_0 binary_to_bcd_2_0_2 (
    .LSB(_7), .O2(binary_to_bcd_2_0_3_lsbf), .O3(binary_to_bcd_2_0_3_o2f), .O4(binary_to_bcd_2_0_3_o3f),
    .LSBF(binary_to_bcd_2_0_2_lsbf), .O2F(binary_to_bcd_2_0_2_o2f), .O3F(binary_to_bcd_2_0_2_o3f),
    .O4F(binary_to_bcd_2_0_2_o4f));
  Binary_to_bcd_2_0 binary_to_bcd_2_0_3 (
    .LSB(_8), .O2(binary_to_bcd_2_0_1_lsbf), .O3(binary_to_bcd_2_0_1_o2f), .O4(binary_to_bcd_2_0_1_o3f),
    .LSBF(binary_to_bcd_2_0_3_lsbf), .O2F(binary_to_bcd_2_0_3_o2f), .O3F(binary_to_bcd_2_0_3_o3f),
    .O4F(binary_to_bcd_2_0_3_o4f));
  Binary_to_bcd_2_0 binary_to_bcd_2_0_4 (
    .LSB(_4), .O2(binary_to_bcd_2_0_5_lsbf), .O3(binary_to_bcd_2_0_5_o2f), .O4(binary_to_bcd_2_0_5_o3f),
    .LSBF(binary_to_bcd_2_0_4_lsbf), .O2F(binary_to_bcd_2_0_4_o2f), .O3F(binary_to_bcd_2_0_4_o3f),
    .O4F(binary_to_bcd_2_0_4_o4f));
  Binary_to_bcd_2_0 binary_to_bcd_2_0_5 (
    .LSB(_5), .O2(binary_to_bcd_2_0_6_lsbf), .O3(binary_to_bcd_2_0_6_o2f), .O4(binary_to_bcd_2_0_6_o3f),
    .LSBF(binary_to_bcd_2_0_5_lsbf), .O2F(binary_to_bcd_2_0_5_o2f), .O3F(binary_to_bcd_2_0_5_o3f),
    .O4F(binary_to_bcd_2_0_5_o4f));
  Binary_to_bcd_2_0 binary_to_bcd_2_0_6 (
    .LSB(_6), .O2(binary_to_bcd_2_0_2_lsbf), .O3(binary_to_bcd_2_0_2_o2f), .O4(binary_to_bcd_2_0_2_o3f),
    .LSBF(binary_to_bcd_2_0_6_lsbf), .O2F(binary_to_bcd_2_0_6_o2f), .O3F(binary_to_bcd_2_0_6_o3f),
    .O4F(binary_to_bcd_2_0_6_o4f));
  Binary_to_bcd_2_0 binary_to_bcd_2_0_7 (
    .LSB(binary_to_bcd_2_0_5_o4f), .O2(binary_to_bcd_2_0_8_lsbf), .O3(binary_to_bcd_2_0_8_o2f),
    .O4(binary_to_bcd_2_0_8_o3f), .LSBF(binary_to_bcd_2_0_7_lsbf), .O2F(binary_to_bcd_2_0_7_o2f),
    .O3F(binary_to_bcd_2_0_7_o3f), .O4F(binary_to_bcd_2_0_7_o4f));
  Binary_to_bcd_2_0 binary_to_bcd_2_0_8 (
    .LSB(binary_to_bcd_2_0_6_o4f), .O2(binary_to_bcd_2_0_2_o4f), .O3(binary_to_bcd_2_0_3_o4f),
    .O4(binary_to_bcd_2_0_1_o4f), .LSBF(binary_to_bcd_2_0_8_lsbf), .O2F(binary_to_bcd_2_0_8_o2f),
    .O3F(binary_to_bcd_2_0_8_o3f), .O4F(binary_to_bcd_2_0_8_o4f));
  Binary_to_bcd_2_0 binary_to_bcd_2_0_9 (
    .LSB(_1), .O2(binary_to_bcd_2_0_10_lsbf), .O3(binary_to_bcd_2_0_10_o2f), .O4(binary_to_bcd_2_0_10_o3f),
    .LSBF(binary_to_bcd_2_0_9_lsbf), .O2F(binary_to_bcd_2_0_9_o2f), .O3F(binary_to_bcd_2_0_9_o3f),
    .O4F(binary_to_bcd_2_0_9_o4f));
  Binary_to_bcd_2_0 binary_to_bcd_2_0_10 (
    .LSB(_2), .O2(binary_to_bcd_2_0_11_lsbf), .O3(binary_to_bcd_2_0_11_o2f), .O4(binary_to_bcd_2_0_11_o3f),
    .LSBF(binary_to_bcd_2_0_10_lsbf), .O2F(binary_to_bcd_2_0_10_o2f), .O3F(binary_to_bcd_2_0_10_o3f),
    .O4F(binary_to_bcd_2_0_10_o4f));
  Binary_to_bcd_2_0 binary_to_bcd_2_0_11 (
    .LSB(_3), .O2(binary_to_bcd_2_0_4_lsbf), .O3(binary_to_bcd_2_0_4_o2f), .O4(binary_to_bcd_2_0_4_o3f),
    .LSBF(binary_to_bcd_2_0_11_lsbf), .O2F(binary_to_bcd_2_0_11_o2f), .O3F(binary_to_bcd_2_0_11_o3f),
    .O4F(binary_to_bcd_2_0_11_o4f));
  Binary_to_bcd_2_0 binary_to_bcd_2_0_12 (
    .LSB(binary_to_bcd_2_0_10_o4f), .O2(binary_to_bcd_2_0_13_lsbf), .O3(binary_to_bcd_2_0_13_o2f),
    .O4(binary_to_bcd_2_0_13_o3f), .LSBF(binary_to_bcd_2_0_12_lsbf), .O2F(binary_to_bcd_2_0_12_o2f),
    .O3F(binary_to_bcd_2_0_12_o3f), .O4F(binary_to_bcd_2_0_12_o4f));
  Binary_to_bcd_2_0 binary_to_bcd_2_0_13 (
    .LSB(binary_to_bcd_2_0_11_o4f), .O2(binary_to_bcd_2_0_14_lsbf), .O3(binary_to_bcd_2_0_14_o2f),
    .O4(binary_to_bcd_2_0_14_o3f), .LSBF(binary_to_bcd_2_0_13_lsbf), .O2F(binary_to_bcd_2_0_13_o2f),
    .O3F(binary_to_bcd_2_0_13_o3f), .O4F(binary_to_bcd_2_0_13_o4f));
  Binary_to_bcd_2_0 binary_to_bcd_2_0_14 (
    .LSB(binary_to_bcd_2_0_4_o4f), .O2(binary_to_bcd_2_0_7_lsbf), .O3(binary_to_bcd_2_0_7_o2f),
    .O4(binary_to_bcd_2_0_7_o3f), .LSBF(binary_to_bcd_2_0_14_lsbf), .O2F(binary_to_bcd_2_0_14_o2f),
    .O3F(binary_to_bcd_2_0_14_o3f), .O4F(binary_to_bcd_2_0_14_o4f));
  Binary_to_bcd_2_0 binary_to_bcd_2_0_15 (
    .LSB(binary_to_bcd_2_0_13_o4f), .O2(binary_to_bcd_2_0_14_o4f), .O3(binary_to_bcd_2_0_7_o4f),
    .O4(binary_to_bcd_2_0_8_o4f), .LSBF(binary_to_bcd_2_0_15_lsbf), .O2F(binary_to_bcd_2_0_15_o2f),
    .O3F(binary_to_bcd_2_0_15_o3f));  // open: O4F
  _7_Seg__Displ_Fuk u_7_seg_displ_fuk_1 (
    .O4(binary_to_bcd_2_0_9_o3f), .O3(binary_to_bcd_2_0_9_o2f), .O2(binary_to_bcd_2_0_9_lsbf), .LSB(_0),
    .a(aU), .b(bU), .c(cU), .d(dU), .e(eU), .f(fU), .g(gU));
  _7_Seg__Displ u_7_seg_displ_1 (
    .O4(binary_to_bcd_2_0_12_o3f), .O3(binary_to_bcd_2_0_12_o2f), .a(aD), .O2(binary_to_bcd_2_0_12_lsbf),
    .LSB(binary_to_bcd_2_0_9_o4f), .b(bD), .c(cD), .d(dD), .e(eD), .f(fD), .g(gD));
  _7_Seg__Displ u_7_seg_displ_2 (
    .O4(binary_to_bcd_2_0_15_o3f), .O3(binary_to_bcd_2_0_15_o2f), .a(aC), .O2(binary_to_bcd_2_0_15_lsbf),
    .LSB(binary_to_bcd_2_0_12_o4f), .b(bC), .c(cC), .d(dC), .e(eC), .f(fC), .g(gC));

  // Notes on the sheet:
  //   UNIDADE
  //   DEZENA
  //   CENTENA
endmodule

module _7_Seg__Displ (
  input  O4,
  input  O3,
  input  O2,
  input  LSB,
  output a,
  output b,
  output c,
  output d,
  output e,
  output f,
  output g
);

  wire and_1_out, and_2_out, and_3_out, and_4_out, and_5_out, and_6_out, and_7_out, and_8_out, and_9_out,
       and_10_out, and_11_out, and_12_out, and_13_out, and_14_out, and_15_out, and_16_out, and_17_out,
       and_18_out, and_19_out, and_20_out, and_21_out, and_22_out, and_23_out, and_24_out, and_25_out,
       and_26_out, and_27_out, not_1_out, not_2_out, not_3_out, not_4_out, not_5_out, not_6_out, not_7_out,
       not_8_out, not_9_out, not_10_out, not_11_out, not_12_out, not_13_out, not_14_out, not_15_out,
       not_16_out, not_17_out, not_18_out, not_19_out, not_20_out, not_21_out, not_22_out, not_23_out,
       not_24_out, not_25_out, not_26_out, not_27_out, not_28_out, not_29_out, not_30_out, not_31_out,
       not_32_out, not_33_out;

  not not_1 (not_1_out, O3);
  and and_1 (and_1_out, not_1_out, not_2_out);
  not not_2 (not_2_out, LSB);
  and and_2 (and_2_out, O3, LSB);
  not not_3 (not_3_out, O4);
  and and_3 (and_3_out, not_3_out, not_4_out);
  not not_4 (not_4_out, O3);
  not not_5 (not_5_out, O4);
  and and_4 (and_4_out, not_5_out, not_6_out, not_7_out);
  not not_6 (not_6_out, O2);
  not not_7 (not_7_out, LSB);
  not not_8 (not_8_out, O3);
  and and_5 (and_5_out, not_8_out, LSB);
  not not_9 (not_9_out, O3);
  and and_6 (and_6_out, not_9_out, O2);
  and and_7 (and_7_out, O2, LSB);
  and and_8 (and_8_out, O4, O3);
  not not_10 (not_10_out, O2);
  not not_11 (not_11_out, O3);
  not not_12 (not_12_out, O2);
  and and_9 (and_9_out, not_11_out, not_12_out, not_13_out);
  not not_13 (not_13_out, LSB);
  not not_14 (not_14_out, O4);
  and and_10 (and_10_out, not_14_out, O2, not_15_out);
  not not_15 (not_15_out, LSB);
  not not_16 (not_16_out, O3);
  and and_11 (and_11_out, not_16_out, O2, LSB);
  and and_12 (and_12_out, O3, not_17_out, LSB);
  not not_17 (not_17_out, O2);
  and and_13 (and_13_out, O4, not_18_out, not_19_out);
  not not_18 (not_18_out, O2);
  not not_19 (not_19_out, LSB);
  and and_14 (and_14_out, O4, O3, LSB);
  not not_20 (not_20_out, O4);
  not not_21 (not_21_out, O3);
  and and_15 (and_15_out, not_20_out, not_21_out, not_22_out);
  not not_22 (not_22_out, LSB);
  not not_23 (not_23_out, O4);
  and and_16 (and_16_out, not_23_out, O2, not_24_out);
  not not_24 (not_24_out, LSB);
  and and_17 (and_17_out, O4, O2, LSB);
  and and_18 (and_18_out, O4, O3, LSB);
  not not_25 (not_25_out, O2);
  and and_19 (and_19_out, not_25_out, not_26_out);
  not not_26 (not_26_out, LSB);
  and and_20 (and_20_out, O3, not_27_out);
  not not_27 (not_27_out, O2);
  and and_21 (and_21_out, O3, not_28_out);
  not not_28 (not_28_out, LSB);
  and and_22 (and_22_out, O4, LSB);
  not not_29 (not_29_out, O4);
  and and_23 (and_23_out, not_29_out, not_30_out, O2);
  not not_30 (not_30_out, O3);
  and and_24 (and_24_out, O3, not_31_out);
  not not_31 (not_31_out, O2);
  and and_25 (and_25_out, O3, not_32_out);
  not not_32 (not_32_out, LSB);
  and and_26 (and_26_out, O4, not_33_out);
  not not_33 (not_33_out, O2);
  and and_27 (and_27_out, O4, LSB);
  or or_1 (a, and_1_out, O2, and_2_out, O4);
  or or_2 (c, not_10_out, LSB, O3, O4);
  or or_3 (e, and_15_out, and_16_out, and_17_out, and_18_out);
  or or_4 (f, and_19_out, and_20_out, and_21_out, and_22_out);
  or or_5 (g, and_23_out, and_24_out, and_25_out, and_26_out, and_27_out);
  or or_6 (b, and_3_out, and_4_out, and_5_out, and_6_out, and_7_out, and_8_out);
  or or_7 (d, and_9_out, and_10_out, and_11_out, and_12_out, and_13_out, and_14_out);
endmodule

module Binary_to_bcd (
  input  O4,
  input  O3,
  input  O2,
  input  LSB,
  output O4F,
  output O3F,
  output O2F,
  output LSBF
);

  wire and_1_out, and_2_out, and_3_out, and_4_out, and_5_out, and_6_out, and_7_out, and_8_out, and_9_out,
       and_10_out, and_11_out, and_12_out, not_1_out, not_2_out, not_3_out, not_4_out, not_5_out, not_6_out,
       not_7_out, not_8_out;

  and and_1 (and_1_out, O3, LSB);
  and and_2 (and_2_out, O3, O2);
  and and_3 (and_3_out, O3, not_1_out, not_2_out);
  not not_1 (not_1_out, O2);
  not not_2 (not_2_out, LSB);
  and and_4 (and_4_out, O4, LSB);
  and and_5 (and_5_out, O4, O3);
  not not_3 (not_3_out, O3);
  and and_6 (and_6_out, not_3_out, O2);
  and and_7 (and_7_out, O2, LSB);
  and and_8 (and_8_out, O4, not_4_out);
  not not_4 (not_4_out, LSB);
  not not_5 (not_5_out, O4);
  and and_9 (and_9_out, not_5_out, not_6_out, LSB);
  not not_6 (not_6_out, O3);
  and and_10 (and_10_out, O3, O2, not_7_out);
  not not_7 (not_7_out, LSB);
  and and_11 (and_11_out, O4, not_8_out);
  not not_8 (not_8_out, LSB);
  and and_12 (and_12_out, O4, O3);
  or or_1 (O4F, and_1_out, and_2_out, O4);
  or or_2 (O3F, and_3_out, and_4_out, and_5_out);
  or or_3 (O2F, and_6_out, and_7_out, and_8_out);
  or or_4 (LSBF, and_9_out, and_10_out, and_11_out, and_12_out);
endmodule

module Binary_to_bcd_2_0 (
  input  LSB,
  input  O2,
  input  O3,
  input  O4,
  output LSBF,
  output O2F,
  output O3F,
  output O4F
);

  wire and_1_out, and_2_out, and_3_out, and_4_out, and_5_out, and_6_out, and_7_out, and_8_out, and_9_out,
       and_10_out, not_1_out, not_2_out, not_3_out, not_4_out, not_5_out, not_6_out, not_7_out, not_8_out;

  not not_1 (not_1_out, LSB);
  and and_1 (and_1_out, not_1_out, O4);
  not not_2 (not_2_out, LSB);
  and and_2 (and_2_out, not_2_out, O2, O3);
  and and_3 (and_3_out, LSB, not_3_out, not_4_out);
  not not_3 (not_3_out, O3);
  not not_4 (not_4_out, O4);
  not not_5 (not_5_out, LSB);
  and and_4 (and_4_out, not_5_out, O4);
  and and_5 (and_5_out, O2, not_6_out);
  not not_6 (not_6_out, O3);
  and and_6 (and_6_out, LSB, O2);
  not not_7 (not_7_out, LSB);
  and and_7 (and_7_out, not_7_out, not_8_out, O3);
  not not_8 (not_8_out, O2);
  and and_8 (and_8_out, LSB, O4);
  and and_9 (and_9_out, O2, O3);
  and and_10 (and_10_out, LSB, O3);
  or or_1 (LSBF, and_1_out, and_2_out, and_3_out);
  or or_2 (O2F, and_4_out, and_5_out, and_6_out);
  or or_3 (O3F, and_7_out, and_8_out);
  or or_4 (O4F, O4, and_9_out, and_10_out);
endmodule

module _7_Seg__Displ_Fuk (
  input  O4,
  input  O3,
  input  O2,
  input  LSB,
  output a,
  output b,
  output c,
  output d,
  output e,
  output f,
  output g
);

  wire and_1_out, and_2_out, and_3_out, and_4_out, and_5_out, and_6_out, and_7_out, and_8_out, and_9_out,
       and_10_out, and_11_out, and_12_out, and_13_out, and_14_out, and_15_out, and_16_out, and_17_out,
       and_18_out, and_19_out, and_20_out, and_21_out, and_22_out, and_23_out, not_1_out, not_2_out,
       not_3_out, not_4_out, not_5_out, not_6_out, not_7_out, not_8_out, not_9_out, not_10_out, not_11_out,
       not_12_out, not_13_out, not_14_out, not_15_out, not_16_out, not_17_out, not_18_out, not_19_out,
       not_20_out, not_21_out, not_22_out, not_23_out, not_24_out, not_25_out, not_26_out, not_27_out,
       not_28_out, not_29_out;

  not not_1 (not_1_out, O3);
  and and_1 (and_1_out, not_1_out, not_2_out);
  not not_2 (not_2_out, LSB);
  and and_2 (and_2_out, O3, LSB);
  not not_3 (not_3_out, O3);
  not not_4 (not_4_out, O2);
  and and_3 (and_3_out, not_4_out, not_5_out);
  not not_5 (not_5_out, LSB);
  and and_4 (and_4_out, O2, LSB);
  not not_6 (not_6_out, O2);
  not not_7 (not_7_out, O3);
  and and_5 (and_5_out, not_7_out, not_8_out, not_9_out);
  not not_8 (not_8_out, O2);
  not not_9 (not_9_out, LSB);
  not not_10 (not_10_out, O4);
  and and_6 (and_6_out, not_10_out, O2, not_11_out);
  not not_11 (not_11_out, LSB);
  not not_12 (not_12_out, O3);
  and and_7 (and_7_out, not_12_out, O2, LSB);
  and and_8 (and_8_out, O3, not_13_out, LSB);
  not not_13 (not_13_out, O2);
  not not_14 (not_14_out, O2);
  and and_9 (and_9_out, O4, not_14_out, not_15_out);
  not not_15 (not_15_out, LSB);
  and and_10 (and_10_out, O4, O3, LSB);
  not not_16 (not_16_out, O3);
  not not_17 (not_17_out, O2);
  and and_11 (and_11_out, not_16_out, not_17_out, not_18_out);
  not not_18 (not_18_out, LSB);
  not not_19 (not_19_out, O4);
  and and_12 (and_12_out, not_19_out, O2, not_20_out);
  not not_20 (not_20_out, LSB);
  and and_13 (and_13_out, O4, O2, LSB);
  and and_14 (and_14_out, O4, O3, LSB);
  not not_21 (not_21_out, O2);
  and and_15 (and_15_out, not_21_out, not_22_out);
  not not_22 (not_22_out, LSB);
  and and_16 (and_16_out, O3, not_23_out);
  not not_23 (not_23_out, O2);
  and and_17 (and_17_out, O3, not_24_out);
  not not_24 (not_24_out, LSB);
  and and_18 (and_18_out, O4, LSB);
  not not_25 (not_25_out, O4);
  not not_26 (not_26_out, O3);
  and and_19 (and_19_out, not_25_out, not_26_out, O2);
  and and_20 (and_20_out, O3, not_27_out);
  not not_27 (not_27_out, O2);
  and and_21 (and_21_out, O3, not_28_out);
  not not_28 (not_28_out, LSB);
  and and_22 (and_22_out, O4, not_29_out);
  not not_29 (not_29_out, O2);
  and and_23 (and_23_out, O4, LSB);
  or or_1 (a, and_1_out, O2, and_2_out, O4);
  or or_2 (b, not_3_out, and_3_out, and_4_out, O4);
  or or_3 (c, not_6_out, LSB, O3, O4);
  or or_4 (e, and_11_out, and_12_out, and_13_out, and_14_out);
  or or_5 (f, and_15_out, and_16_out, and_17_out, and_18_out);
  or or_6 (g, and_19_out, and_20_out, and_21_out, and_22_out, and_23_out);
  or or_7 (d, and_5_out, and_6_out, and_7_out, and_8_out, and_9_out, and_10_out);
endmodule
