// Logisim project TrabalhoCD.circ as structural Verilog: 5 circuits, main circuit main
module main (
  input  [4:0] A,
  input  [4:0] B,
  output out_3,
  output out_4,
  output out_5,
  output out_6,
  output out_7,
  output out_8,
  output out_9,
  output out_10,
  output out_11,
  output out_12
);

  wire AA, AA1, AA2, AA3, AA4, AA5, AA6, AB, AC, AD, AE, BA, BA1, BA2, BA3, BA4, BA5, BA6, BB, BC, BD, BE,
       CA, CA1, CA2, CA3, CA4, CA5, CA6, CB, CC, CD, CE, DA, DB, DC, DD, DE, EA, EB, EC, ED, EE;

  Multiplicator multiplicator_1 (
    .IN0(A[0]), .IN1(B[0]), .IN2(B[1]), .IN3(B[2]), .IN4(B[3]), .IN5(B[4]), .OUT5(AA), .OUT4(AB), .OUT3(AC),
    .OUT2(AD), .OUT1(AE));
  Multiplicator multiplicator_2 (
    .IN0(A[1]), .IN1(B[0]), .IN2(B[1]), .IN3(B[2]), .IN4(B[3]), .IN5(B[4]), .OUT5(BA), .OUT4(BB), .OUT3(BC),
    .OUT2(BD), .OUT1(BE));
  Multiplicator multiplicator_3 (
    .IN0(A[2]), .IN1(B[0]), .IN2(B[1]), .IN3(B[2]), .IN4(B[3]), .IN5(B[4]), .OUT5(CA), .OUT4(CB), .OUT3(CC),
    .OUT2(CD), .OUT1(CE));
  Multiplicator multiplicator_4 (
    .IN0(A[3]), .IN1(B[0]), .IN2(B[1]), .IN3(B[2]), .IN4(B[3]), .IN5(B[4]), .OUT5(DA), .OUT4(DB), .OUT3(DC),
    .OUT2(DD), .OUT1(DE));
  Multiplicator multiplicator_5 (
    .IN0(A[4]), .IN1(B[0]), .IN2(B[1]), .IN3(B[2]), .IN4(B[3]), .IN5(B[4]), .OUT5(EA), .OUT4(EB), .OUT3(EC),
    .OUT2(ED), .OUT1(EE));
  Sum sum_1 (
    .IN00(AA), .IN01(AB), .IN02(AC), .IN03(AD), .IN04(AE), .IN05(1'b0), .IN11(BA), .IN12(BB), .IN13(BC),
    .IN14(BD), .IN15(BE), .F_OUT(out_3), ._1_OUT(AA1), ._2_OUT(AA2), ._3_OUT(AA3), ._4_OUT(AA4),
    ._5_OUT(AA5), ._6_OUT(AA6));
  Sum sum_2 (
    .IN00(AA1), .IN01(AA2), .IN02(AA3), .IN03(AA4), .IN04(AA5), .IN05(AA6), .IN11(CA), .IN12(CB), .IN13(CC),
    .IN14(CD), .IN15(CE), .F_OUT(out_4), ._1_OUT(BA1), ._2_OUT(BA2), ._3_OUT(BA3), ._4_OUT(BA4),
    ._5_OUT(BA5), ._6_OUT(BA6));
  Sum sum_3 (
    .IN00(BA1), .IN01(BA2), .IN02(BA3), .IN03(BA4), .IN04(BA5), .IN05(BA6), .IN11(DA), .IN12(DB), .IN13(DC),
    .IN14(DD), .IN15(DE), .F_OUT(out_5), ._1_OUT(CA1), ._2_OUT(CA2), ._3_OUT(CA3), ._4_OUT(CA4),
    ._5_OUT(CA5), ._6_OUT(CA6));
  Sum sum_4 (
    .IN00(CA1), .IN01(CA2), .IN02(CA3), .IN03(CA4), .IN04(CA5), .IN05(CA6), .IN11(EA), .IN12(EB), .IN13(EC),
    .IN14(ED), .IN15(EE), .F_OUT(out_6), ._1_OUT(out_7), ._2_OUT(out_8), ._3_OUT(out_9), ._4_OUT(out_10),
    ._5_OUT(out_11), ._6_OUT(out_12));

  // Other names for the same wires on the sheet: A1 = A[0]; A2 = A[1]; A3 = A[2]; A4 = A[3]; A5 = A[4]; B1 = B[0];
  //   B2 = B[1]; B3 = B[2]; B4 = B[3]; B5 = B[4]; OUT_A = out_3; OUT_B = out_4; OUT_C = out_5; OUT_D = out_6;
  //   OUT_E = out_7; OUT_F = out_8; OUT_G = out_9; OUT_H = out_10; OUT_I = out_11; OUT_J = out_12
endmodule

// S
module Sum (
  input  IN00,
  input  IN01,
  input  IN02,
  input  IN03,
  input  IN04,
  input  IN05,
  input  IN11,
  input  IN12,
  input  IN13,
  input  IN14,
  input  IN15,
  output F_OUT,
  output _1_OUT,
  output _2_OUT,
  output _3_OUT,
  output _4_OUT,
  output _5_OUT,
  output _6_OUT
);

  wire full_adder_1_carry_out, full_adder_2_carry_out, full_adder_3_carry_out, half_adder_1_p1;

  Half_Adder half_adder_1 (.A(IN01), .B(IN11), .P0(_1_OUT), .P1(half_adder_1_p1));
  Full_Adder full_adder_1 (
    .Carry_IN(half_adder_1_p1), .A(IN02), .B(IN12), .S(_2_OUT), .Carry_OUT(full_adder_1_carry_out));
  Full_Adder full_adder_2 (
    .Carry_IN(full_adder_1_carry_out), .A(IN03), .B(IN13), .S(_3_OUT), .Carry_OUT(full_adder_2_carry_out));
  Full_Adder full_adder_3 (
    .Carry_IN(full_adder_2_carry_out), .A(IN04), .B(IN14), .S(_4_OUT), .Carry_OUT(full_adder_3_carry_out));
  Full_Adder full_adder_4 (.Carry_IN(full_adder_3_carry_out), .A(IN05), .B(IN15), .S(_5_OUT), .Carry_OUT(_6_OUT));

  assign F_OUT = IN00;
endmodule

module Multiplicator (
  input  IN0,
  input  IN1,
  input  IN2,
  input  IN3,
  input  IN4,
  input  IN5,
  output OUT5,
  output OUT4,
  output OUT3,
  output OUT2,
  output OUT1
);

  and and_1 (OUT1, IN1, IN0);
  and and_2 (OUT2, IN2, IN0);
  and and_3 (OUT3, IN3, IN0);
  and and_4 (OUT4, IN4, IN0);
  and and_5 (OUT5, IN5, IN0);
endmodule

module Half_Adder (
  input  A,
  input  B,
  output P0,
  output P1
);

  xor xor_1 (P0, A, B);
  and and_1 (P1, A, B);
endmodule

module Full_Adder (
  input  Carry_IN,
  input  A,
  input  B,
  output S,
  output Carry_OUT
);

  wire and_1_out, and_2_out, xor_1_out;

  and and_1 (and_1_out, A, B);
  xor xor_1 (xor_1_out, A, B);
  xor xor_2 (S, Carry_IN, xor_1_out);
  and and_2 (and_2_out, Carry_IN, xor_1_out);
  or or_1 (Carry_OUT, and_2_out, and_1_out);
endmodule
