// Logisim project TrabalhoCD_FUNC.circ as structural Verilog: 5 circuits, main circuit main
module main (
  input  [4:0] B,
  input  [4:0] A,
  output out_3,
  output out_4,
  output out_5,
  output out_6,
  output out_7,
  output out_8,
  output out_9,
  output out_10,
  output out_11,
  output out_12
);

  wire Carry_S1, Carry_S2, Carry_S3, LSB_M1, LSB_M2, LSB_M3, LSB_M4, LSB_M5, M12, M13, M14, M22, M23, M24,
       M32, M33, M34, M42, M43, M44, M52, M53, M54, MSB_M1, MSB_M2, MSB_M3, MSB_M4, MSB_M5, MSB_S1, MSB_S2,
       MSB_S3, S12, S13, S14, S15, S22, S23, S24, S25, S32, S33, S34, S35;

  Multiplicator multiplicator_1 (
    .IN0(A[0]), .IN1(B[0]), .IN2(B[1]), .IN3(B[2]), .IN4(B[3]), .IN5(B[4]), .OUT5(MSB_M1), .OUT4(M14),
    .OUT3(M13), .OUT2(M12), .OUT1(LSB_M1));
  Multiplicator multiplicator_2 (
    .IN0(A[1]), .IN1(B[0]), .IN2(B[1]), .IN3(B[2]), .IN4(B[3]), .IN5(B[4]), .OUT5(MSB_M2), .OUT4(M24),
    .OUT3(M23), .OUT2(M22), .OUT1(LSB_M2));
  Multiplicator multiplicator_3 (
    .IN0(A[2]), .IN1(B[0]), .IN2(B[1]), .IN3(B[2]), .IN4(B[3]), .IN5(B[4]), .OUT5(MSB_M3), .OUT4(M34),
    .OUT3(M33), .OUT2(M32), .OUT1(LSB_M3));
  Multiplicator multiplicator_4 (
    .IN0(A[3]), .IN1(B[0]), .IN2(B[1]), .IN3(B[2]), .IN4(B[3]), .IN5(B[4]), .OUT5(MSB_M4), .OUT4(M44),
    .OUT3(M43), .OUT2(M42), .OUT1(LSB_M4));
  Multiplicator multiplicator_5 (
    .IN0(A[4]), .IN1(B[0]), .IN2(B[1]), .IN3(B[2]), .IN4(B[3]), .IN5(B[4]), .OUT5(MSB_M5), .OUT4(M54),
    .OUT3(M53), .OUT2(M52), .OUT1(LSB_M5));
  Sum sum_1 (
    .IN00(LSB_M1), .IN01(M12), .IN02(M13), .IN03(M14), .IN04(MSB_M1), .IN05(1'b0), .IN11(LSB_M2), .IN12(M22),
    .IN13(M23), .IN14(M24), .IN15(MSB_M2), .F_OUT(out_12), ._1_OUT(S12), ._2_OUT(S13), ._3_OUT(S14),
    ._4_OUT(S15), ._5_OUT(MSB_S1), ._6_OUT(Carry_S1));
  Sum sum_2 (
    .IN00(S12), .IN01(S13), .IN02(S14), .IN03(S15), .IN04(MSB_S1), .IN05(Carry_S1), .IN11(LSB_M3),
    .IN12(M32), .IN13(M33), .IN14(M34), .IN15(MSB_M3), .F_OUT(out_11), ._1_OUT(S22), ._2_OUT(S23),
    ._3_OUT(S24), ._4_OUT(S25), ._5_OUT(MSB_S2), ._6_OUT(Carry_S2));
  Sum sum_3 (
    .IN00(S22), .IN01(S23), .IN02(S24), .IN03(S25), .IN04(MSB_S2), .IN05(Carry_S2), .IN11(LSB_M4),
    .IN12(M42), .IN13(M43), .IN14(M44), .IN15(MSB_M4), .F_OUT(out_10), ._1_OUT(S32), ._2_OUT(S33),
    ._3_OUT(S34), ._4_OUT(S35), ._5_OUT(MSB_S3), ._6_OUT(Carry_S3));
  Sum sum_4 (
    .IN00(S32), .IN01(S33), .IN02(S34), .IN03(S35), .IN04(MSB_S3), .IN05(Carry_S3), .IN11(LSB_M5),
    .IN12(M52), .IN13(M53), .IN14(M54), .IN15(MSB_M5), .F_OUT(out_9), ._1_OUT(out_8), ._2_OUT(out_7),
    ._3_OUT(out_6), ._4_OUT(out_5), ._5_OUT(out_4), ._6_OUT(out_3));

  // Other names for the same wires on the sheet: LSB_A = A[0]; A2 = A[1]; A3 = A[2]; A4 = A[3]; MSB_A = A[4];
  //   LSB_B = B[0]; B2 = B[1]; B3 = B[2]; B4 = B[3]; MSB_B = B[4]; LSB = out_12; MSB = out_3; O2 = out_11;
  //   O3 = out_10; O4 = out_9; O5 = out_8; O6 = out_7; O7 = out_6; O8 = out_5; O9 = out_4
endmodule

// S
module Sum (
  input  IN00,
  input  IN01,
  input  IN02,
  input  IN03,
  input  IN04,
  input  IN05,
  input  IN11,
  input  IN12,
  input  IN13,
  input  IN14,
  input  IN15,
  output F_OUT,
  output _1_OUT,
  output _2_OUT,
  output _3_OUT,
  output _4_OUT,
  output _5_OUT,
  output _6_OUT
);

  wire full_adder_1_carry_out, full_adder_2_carry_out, full_adder_3_carry_out, half_adder_1_p1;

  Half_Adder half_adder_1 (.A(IN01), .B(IN11), .P0(_1_OUT), .P1(half_adder_1_p1));
  Full_Adder full_adder_1 (
    .Carry_IN(half_adder_1_p1), .A(IN02), .B(IN12), .S(_2_OUT), .Carry_OUT(full_adder_1_carry_out));
  Full_Adder full_adder_2 (
    .Carry_IN(full_adder_1_carry_out), .A(IN03), .B(IN13), .S(_3_OUT), .Carry_OUT(full_adder_2_carry_out));
  Full_Adder full_adder_3 (
    .Carry_IN(full_adder_2_carry_out), .A(IN04), .B(IN14), .S(_4_OUT), .Carry_OUT(full_adder_3_carry_out));
  Full_Adder full_adder_4 (.Carry_IN(full_adder_3_carry_out), .A(IN05), .B(IN15), .S(_5_OUT), .Carry_OUT(_6_OUT));

  assign F_OUT = IN00;
endmodule

module Multiplicator (
  input  IN0,
  input  IN1,
  input  IN2,
  input  IN3,
  input  IN4,
  input  IN5,
  output OUT5,
  output OUT4,
  output OUT3,
  output OUT2,
  output OUT1
);

  and and_1 (OUT1, IN1, IN0);
  and and_2 (OUT2, IN2, IN0);
  and and_3 (OUT3, IN3, IN0);
  and and_4 (OUT4, IN4, IN0);
  and and_5 (OUT5, IN5, IN0);
endmodule

module Half_Adder (
  input  A,
  input  B,
  output P0,
  output P1
);

  xor xor_1 (P0, A, B);
  and and_1 (P1, A, B);
endmodule

module Full_Adder (
  input  Carry_IN,
  input  A,
  input  B,
  output S,
  output Carry_OUT
);

  wire and_1_out, and_2_out, xor_1_out;

  and and_1 (and_1_out, A, B);
  xor xor_1 (xor_1_out, A, B);
  xor xor_2 (S, Carry_IN, xor_1_out);
  and and_2 (and_2_out, Carry_IN, xor_1_out);
  or or_1 (Carry_OUT, and_2_out, and_1_out);
endmodule
